# Fritzing sketch project2 (saved by Fritzing 0.9.3b)
circuit board: 8.46667cm x 5.64444cm
breadboards: 1

parts:
  Part1 = Arduino Uno (Rev3) - ICSP
  R1 = Resistor [tolerance=±5% resistance=2.2k package=THT]
  R2 = Resistor [tolerance=±5% resistance=2.2k package=THT]
  DHT1 = DHT11 Humitidy and Temperature Sensor

nets (from the schematic view):
  5V: Part1.5V, R2.Pin_1, DHT1.VDD
  GND: Part1.GND, DHT1.GND
  N1: Part1.D12/MISO, R1.Pin_0, DHT1.DATA
  N2: R1.Pin_1, R2.Pin_0

custom parts:
  DHT11 Humitidy and Temperature Sensor: DHT11 Humidity and Temperature Sensor
